# Fritzing sketch breadboard_diag (saved by Fritzing 0.9.3b)
breadboards: 1

parts:
  Launchpad1 = TI Launchpad TM4C123GXL
  S1 = Pushbutton [package="[SMD]"]
  S2 = Pushbutton [package="[SMD]"]
  R2 = Resistor [tolerance=±5% resistance=10k package=THT]
  R3 = Resistor [tolerance=±5% resistance=10k package=THT]
  VR1 = Slide Potentiometer
  R4 = Resistor [tolerance=±5% resistance=12k package=THT]
  R5 = Resistor [tolerance=±5% resistance=12k package=THT]
  R6 = Resistor [tolerance=±5% resistance=12k package=THT]
  R7 = Resistor [tolerance=±5% resistance=1.5k package=THT]
  R8 = Resistor [tolerance=±5% resistance=1.5k package=THT]
  R9 = Resistor [tolerance=±5% resistance=1.5k package=THT]
  TRS1 = Audio Jack (TRS) 3.5mm [package="PG203J [THT]"]

nets:
  N1: Launchpad1.PB0, R4.Pin_0
  N2: Launchpad1.PB1, R5.Pin_0, R6.Pin_0
  N3: Launchpad1.PE1, S1.Pin_1, S1.Pin_2, R2.Pin_1
  N4: Launchpad1.PE2, Launchpad1.GND, R2.Pin_0, R3.Pin_0, VR1.A_1, VR1.Wiper_A, TRS1.Sleeve
  N5: Launchpad1.PB3, R9.Pin_0
  N6: Launchpad1.PB2, R7.Pin_0
  N7: Launchpad1.PE0, S2.Pin_1, S2.Pin_2, R3.Pin_1
  N8: Launchpad1.3.3V, S1.Pin_3, S1.Pin_4, S2.Pin_3, S2.Pin_4, VR1.B_2
  N9: R4.Pin_1, R5.Pin_1, R6.Pin_1, R8.Pin_1, R9.Pin_1, TRS1.Tip
  N10: R7.Pin_1, R8.Pin_0

custom parts:
  Slide Potentiometer: 35mm sliding adjustable resistor (potentiometer).
